// Logisim project  seq_circuit.circ as structural Verilog: 1 circuit, main circuit main
module main (
  input  X,
  input  Y,
  output S
);

  wire and_1_out, and_2_out, and_3_out, clock_1_out, d_ff_1_q, not_1_out, or_1_out, xor_1_out, xor_2_out;

  not not_1 (not_1_out, X);
  and and_1 (and_1_out, not_1_out, d_ff_1_q);
  xor xor_1 (xor_1_out, X, Y);
  and and_2 (and_2_out, not_1_out, Y);
  Clock clock_1 (.out(clock_1_out));
  xor xor_2 (xor_2_out, and_2_out, and_1_out);
  D_Flip_Flop d_ff_1 (.clk(clock_1_out), .D(or_1_out), .Q(d_ff_1_q));  // open: Qn, preset, en, reset
  xor xor_3 (S, xor_1_out, d_ff_1_q);
  and and_3 (and_3_out, d_ff_1_q, Y);
  or or_1 (or_1_out, xor_2_out, and_3_out);

  // Notes on the sheet:
  //   Clk
  //   D
  //   Q
  //   C
endmodule
